// Logisim project Part1_7Seg_Decode.circ as structural Verilog: 5 circuits, main circuit main
module main (
  input  v3,
  input  v2,
  input  v1,
  input  v0
);

  wire circuita_1_o0, circuita_1_o1, circuita_1_o2, d0, d1, d2, d3, d4, d5, d6, multiplexer_1_out,
       multiplexer_2_out, multiplexer_3_out, multiplexer_4_out, not_1_out, not_2_out, not_3_out, not_4_out,
       not_5_out, not_6_out, not_7_out, s0, s1, s2, s3, s4, s5, s6, Z;

  CircuitA circuita_1 (.i2(v2), .i1(v1), .i0(v0), .o2(circuita_1_o2), .o1(circuita_1_o1), .o0(circuita_1_o0));
  myComparator mycomparator_1 (.v3(v3), .v2(v2), .v1(v1), .v0(v0), .z(Z));
  Multiplexer multiplexer_1 (.in0(v3), .out(multiplexer_1_out), .sel(Z));  // open: in1
  Multiplexer multiplexer_2 (.in0(v2), .in1(circuita_1_o2), .out(multiplexer_2_out), .sel(Z));
  Multiplexer multiplexer_3 (.in0(v1), .in1(circuita_1_o1), .out(multiplexer_3_out), .sel(Z));
  Multiplexer multiplexer_4 (.in0(v0), .in1(circuita_1_o0), .out(multiplexer_4_out), .sel(Z));
  CircuitB circuitb_1 (.z(Z), .s0(d0), .s1(d1), .s2(d2), .s3(d3), .s4(d4), .s5(d5), .s6(d6));
  segment7 segment7_1 (
    .w3(multiplexer_1_out), .w2(multiplexer_2_out), .w1(multiplexer_3_out), .w0(multiplexer_4_out), .a(s0),
    .b(s1), .c(s2), .d(s3), .e(s4), .f(s5), .g(s6));
  _7_Segment_Display u_7_segment_display_1 (.g(d6), .f(d5), .a(d0), .b(d1), .e(d4), .d(d3), .c(d2));  // open: dp
  not not_1 (not_1_out, s6);
  _7_Segment_Display u_7_segment_display_2 (
    .g(not_1_out), .f(not_4_out), .a(not_5_out), .b(not_6_out), .e(not_2_out), .d(not_3_out), .c(not_7_out));  // open: dp
  not not_2 (not_2_out, s4);
  not not_3 (not_3_out, s3);
  not not_4 (not_4_out, s5);
  not not_5 (not_5_out, s0);
  not not_6 (not_6_out, s1);
  not not_7 (not_7_out, s2);
endmodule

module segment7 (
  input  w3,
  input  w2,
  input  w1,
  input  w0,
  output a,
  output b,
  output c,
  output d,
  output e,
  output f,
  output g
);

  wire and_1_out, and_2_out, and_3_out, and_4_out, and_6_out, and_7_out, and_8_out, and_9_out, and_10_out,
       and_11_out, and_12_out, and_13_out, and_14_out, not_1_out, not_2_out, not_3_out, not_4_out;

  not not_1 (not_1_out, w3);
  not not_2 (not_2_out, w2);
  not not_3 (not_3_out, w1);
  not not_4 (not_4_out, w0);
  and and_1 (and_1_out, not_1_out, not_2_out, not_3_out, w0);
  and and_2 (and_2_out, w2, not_3_out, not_4_out);
  and and_3 (and_3_out, w2, not_3_out, w0);
  and and_4 (and_4_out, w2, w1, not_4_out);
  and and_5 (c, not_2_out, w1, not_4_out);
  and and_6 (and_6_out, not_1_out, not_2_out, not_3_out, w0);
  and and_7 (and_7_out, w2, not_3_out, not_4_out);
  and and_8 (and_8_out, w2, w1, w0);
  and and_9 (and_9_out, w2, not_3_out);
  and and_10 (and_10_out, not_1_out, not_2_out, w0);
  and and_11 (and_11_out, not_2_out, w1);
  and and_12 (and_12_out, w1, w0);
  and and_13 (and_13_out, not_1_out, not_2_out, not_3_out);
  and and_14 (and_14_out, w2, w1, w0);
  or or_1 (a, and_1_out, and_2_out);
  or or_2 (b, and_3_out, and_4_out);
  or or_3 (d, and_6_out, and_7_out, and_8_out);
  or or_4 (e, w0, and_9_out);
  or or_5 (f, and_10_out, and_11_out, and_12_out);
  or or_6 (g, and_13_out, and_14_out);
endmodule

module CircuitA (
  input  i2,
  input  i1,
  input  i0,
  output o2,
  output o1,
  output o0
);

  not not_1 (o1, i1);
  and and_1 (o2, i2, i1);

  assign o0 = i0;
endmodule

module myComparator (
  input  v3,
  input  v2,
  input  v1,
  input  v0,
  output z
);

  wire and_1_out, and_2_out;

  and and_1 (and_1_out, v3, v1, v0);
  and and_2 (and_2_out, v3, v2);
  or or_1 (z, and_1_out, and_2_out);
endmodule

module CircuitB (
  input  z,
  output s0,
  output s1,
  output s2,
  output s3,
  output s4,
  output s5,
  output s6
);

  not not_1 (s1, z);

  assign s0 = 1'b0;
  assign s2 = s1;
  assign s3 = s1;
  assign s4 = 1'b1;
  assign s5 = 1'b1;
  assign s6 = s1;
endmodule
