// Logisim project Part3_RCFA.circ as structural Verilog: 4 circuits, main circuit FA_4
module FA_4 (
  input  a3,
  input  b3,
  input  a2,
  input  b2,
  input  a1,
  input  b1,
  input  cin,
  input  a0,
  input  b0,
  output s3,
  output s2,
  output s1,
  output s0,
  output cout
);

  wire fa_2_co, fa_3_co, fa_4_co;

  FA fa_1 (.b(b3), .a(a3), .ci(fa_2_co), .co(cout), .s(s3));
  FA fa_2 (.b(b2), .a(a2), .ci(fa_3_co), .co(fa_2_co), .s(s2));
  FA fa_3 (.b(b1), .a(a1), .ci(fa_4_co), .co(fa_3_co), .s(s1));
  FA fa_4 (.b(b0), .a(a0), .ci(cin), .co(fa_4_co), .s(s0));
endmodule

module FA (
  input  b,
  input  a,
  input  ci,
  output co,
  output s
);

  wire and_1_out, and_2_out, and_3_out, and_4_out, and_5_out, and_6_out, and_7_out, not_1_out, not_2_out,
       not_3_out;

  not not_1 (not_1_out, b);
  not not_2 (not_2_out, a);
  not not_3 (not_3_out, ci);
  and and_1 (and_1_out, a, ci);
  and and_2 (and_2_out, b, ci);
  and and_3 (and_3_out, b, a);
  and and_4 (and_4_out, not_1_out, not_2_out, ci);
  and and_5 (and_5_out, not_1_out, a, not_3_out);
  and and_6 (and_6_out, b, not_2_out, not_3_out);
  and and_7 (and_7_out, b, a, ci);
  or or_1 (co, and_1_out, and_2_out, and_3_out);
  or or_2 (s, and_4_out, and_5_out, and_6_out, and_7_out);
endmodule

module bcd_FA_4 (
  input  a3,
  input  b3,
  input  a2,
  input  b2,
  input  a1,
  input  b1,
  input  cin,
  input  a0,
  input  b0,
  output t7,
  output t6,
  output t5,
  output t4,
  output t3,
  output t2,
  output t1,
  output t0
);

  wire fa_4_1_cout, fa_4_1_s0, fa_4_1_s1, fa_4_1_s2, fa_4_1_s3;

  FA_4 fa_4_1 (
    .a3(a3), .b3(b3), .a2(a2), .b2(b2), .a1(a1), .b1(b1), .cin(cin), .a0(a0), .b0(b0), .s3(fa_4_1_s3),
    .s2(fa_4_1_s2), .s1(fa_4_1_s1), .s0(fa_4_1_s0), .cout(fa_4_1_cout));
  bin2bcd bin2bcd_1 (
    .s3(fa_4_1_s3), .s2(fa_4_1_s2), .s1(fa_4_1_s1), .s0(fa_4_1_s0), .cout(fa_4_1_cout), .b7(t7), .b6(t6),
    .b5(t5), .b4(t4), .b3(t3), .b2(t2), .b1(t1), .b0(t0));
endmodule

module bin2bcd (
  input  s3,
  input  s2,
  input  s1,
  input  s0,
  input  cout,
  output b7,
  output b6,
  output b5,
  output b4,
  output b3,
  output b2,
  output b1,
  output b0
);

  wire and_1_out, and_2_out, and_3_out, and_4_out, and_5_out, and_6_out, and_7_out, and_8_out, and_9_out,
       and_10_out, and_11_out, and_12_out, and_13_out, and_14_out, and_15_out, and_16_out, and_17_out,
       and_18_out, not_1_out, not_2_out, not_3_out, not_4_out;

  not not_1 (not_1_out, s3);
  not not_2 (not_2_out, s2);
  not not_3 (not_3_out, s1);
  not not_4 (not_4_out, s0);
  and and_1 (and_1_out, s3, s1);
  and and_2 (and_2_out, s3, s2);
  and and_3 (and_3_out, s3, not_2_out, not_3_out);
  and and_4 (and_4_out, not_1_out, s2, s0);
  and and_5 (and_5_out, not_1_out, s2, s1);
  and and_6 (and_6_out, s2, s1, s0);
  and and_7 (and_7_out, s3, not_2_out, not_3_out, s0);
  and and_8 (and_8_out, not_1_out, s2, not_3_out, not_4_out);
  and and_9 (and_9_out, s3, s2, s1, not_4_out);
  and and_10 (and_10_out, s3, not_3_out, not_4_out);
  and and_11 (and_11_out, not_1_out, not_2_out, s1);
  and and_12 (and_12_out, s3, s2, not_3_out);
  and and_13 (and_13_out, not_1_out, s1, s0);
  and and_14 (and_14_out, s3, not_2_out, not_3_out, not_4_out);
  and and_15 (and_15_out, not_1_out, not_2_out, s0);
  and and_16 (and_16_out, not_2_out, s1, s0);
  and and_17 (and_17_out, s3, s2, not_3_out, s0);
  and and_18 (and_18_out, not_1_out, s2, s1, not_4_out);
  or or_1 (b5, and_1_out, and_2_out);
  or or_2 (b4, and_3_out, and_4_out, and_5_out, and_6_out);
  or or_3 (b3, and_7_out, and_8_out, and_9_out);
  or or_4 (b2, and_10_out, and_11_out, and_12_out, and_13_out);
  or or_5 (b1, and_14_out, and_15_out, and_16_out, and_17_out, and_18_out);

  assign b0 = cout;
  assign b6 = 1'b0;
  assign b7 = 1'b0;
endmodule
